# Fritzing sketch remoteIR (saved by Fritzing 0.8.3b)
breadboards: 1

parts:
  Q1 = NPN-Transistor [package="SOT-23 [SMD]"]
  R1 = 47 Ω Resistor [package=THT]
  LED2 = LED - 5mm [color="Infrared (880nm)" package="5 mm [THT]"]
  R2 = 10 Ω Resistor [package=THT]
  Pi1 = Adafruit Pi Cobbler
  Part1 = Arduino Uno (Rev3)

nets:
  GND: Q1.2, Pi1.GND, Part1.GND
  N1: Q1.0, R1.Pin_1
  N2: Q1.1, R2.Pin_1
  N3: R1.Pin_0, Part1.D3_PWM
  N4: LED2.cathode, R2.Pin_0
  N5: LED2.anode, Pi1.5V0, Part1.5V
  N6: Pi1.MOSI, Part1.D11_PWM/MOSI
  N7: Pi1.MISO, Part1.D12/MISO
  N8: Pi1.CE0, Part1.D10_PWM/SS
  N9: Pi1.PIN25, Part1.D13/SCK

custom parts:
  Adafruit Pi Cobbler: Adafruit Pi Cobbler GPIO Breakout for Raspberry Pi
